# Fritzing sketch DS18B20-Holder-x6 (saved by Fritzing 0.9.10b)
circuit board: 5.12528cm x 2.31255cm
breadboards: 1

parts:
  DS2 = DS18B20 1-Wire Temperature Sensor [part_number=DS18B20]
  DS3 = DS18B20 1-Wire Temperature Sensor [part_number=DS18B20]
  DS4 = DS18B20 1-Wire Temperature Sensor [part_number=DS18B20]
  DS5 = DS18B20 1-Wire Temperature Sensor [part_number=DS18B20]
  DS6 = DS18B20 1-Wire Temperature Sensor [part_number=DS18B20]
  R1 = Resistor [tolerance=±20% power=0.5W resistance=4.7k package=THT]
  J2 = male pin header, 3 pins [form="♂ (male)"]
  J1 = screw terminal, 3 pins
  DS1 = DS18B20 1-Wire Temperature Sensor [part_number=DS18B20]

nets:
  GND: DS2.GND, DS3.GND, DS4.GND, DS5.GND, DS6.GND, J2.pin1, J1.pin1, DS1.GND
  N1: DS2.DQ, DS3.DQ, DS4.DQ, DS5.DQ, DS6.DQ, R1.Pin_0, J1.pin2, DS1.DQ
  VDD: DS2.VDD, DS3.VDD, DS4.VDD, DS5.VDD, DS6.VDD, J2.pin2, DS1.VDD
  N2: R1.Pin_1, J2.pin3, J1.pin3

notes:
  ©Adam Howell
  p
  n
  +
  -
